// Logisim project Labo5_Melly_Rouvinez.circ as structural Verilog: 12 circuits, main circuit UART
module COUNT_BASE (
  input  EN,
  input  CLK,
  output Q,
  output C
);

  wire xor_1_out;

  xor xor_1 (xor_1_out, Q, EN);
  and and_1 (C, Q, EN);
  D_Flip_Flop d_ff_1 (.D(xor_1_out), .clk(CLK), .Q(Q));  // open: Qn, preset, reset

  // Notes on the sheet:
  //   Attention, votre version de Logisim
  //   ne contient pas de tracker. Si vous
  //   enregistrez votre projet, toutes les
  //   informations du tracker seront
  //   définitivement effacées.
endmodule

module SHREGI_8BITS (
  input  L,
  input  [1:0] S,
  input  [7:0] D,
  input  R,
  input  CLK,
  output [7:0] Q
);

  wire bitselector_1_out, bitselector_2_out;

  SHREGI_4BITS shregi_4bits_1 (.D(D[3:0]), .R(bitselector_1_out), .L(L), .S(S), .CLK(CLK), .Q(Q[3:0]));
  SHREGI_4BITS shregi_4bits_2 (.D(D[7:4]), .R(R), .L(bitselector_2_out), .S(S), .CLK(CLK), .Q(Q[7:4]));
  BitSelector #(.width(4)) bitselector_1 (.in(Q[7:4]), .out(bitselector_1_out), .sel(2'b00));
  BitSelector #(.width(4)) bitselector_2 (.in(Q[3:0]), .out(bitselector_2_out), .sel(2'b11));

  // Notes on the sheet:
  //   Attention, votre version de Logisim
  //   ne contient pas de tracker. Si vous
  //   enregistrez votre projet, toutes les
  //   informations du tracker seront
  //   définitivement effacées.
endmodule

module SHREGI_4BITS (
  input  [3:0] D,
  input  R,
  input  L,
  input  [1:0] S,
  input  CLK,
  output [3:0] Q
);

  wire multiplexer_1_out, multiplexer_2_out, multiplexer_3_out, multiplexer_4_out;

  Multiplexer #(.select(2), .enable("false")) multiplexer_1 (
    .in0(Q[3]), .in1(D[3]), .in2(Q[2]), .in3(R), .out(multiplexer_1_out), .sel(S));
  D_Flip_Flop d_ff_1 (.D(multiplexer_1_out), .clk(CLK), .Q(Q[3]));  // open: Qn, preset, reset
  Multiplexer #(.select(2), .enable("false")) multiplexer_2 (
    .in0(Q[2]), .in1(D[2]), .in2(Q[1]), .in3(Q[3]), .out(multiplexer_2_out), .sel(S));
  D_Flip_Flop d_ff_2 (.D(multiplexer_2_out), .clk(CLK), .Q(Q[2]));  // open: Qn, preset, reset
  Multiplexer #(.select(2), .enable("false")) multiplexer_3 (
    .in0(Q[1]), .in1(D[1]), .in2(Q[0]), .in3(Q[2]), .out(multiplexer_3_out), .sel(S));
  D_Flip_Flop d_ff_3 (.D(multiplexer_3_out), .clk(CLK), .Q(Q[1]));  // open: Qn, preset, reset
  Multiplexer #(.select(2), .enable("false")) multiplexer_4 (
    .in0(Q[0]), .in1(D[0]), .in2(L), .in3(Q[1]), .out(multiplexer_4_out), .sel(S));
  D_Flip_Flop d_ff_4 (.D(multiplexer_4_out), .clk(CLK), .Q(Q[0]));  // open: Qn, preset, reset

  // Notes on the sheet:
  //   Attention, votre version de Logisim
  //   ne contient pas de tracker. Si vous
  //   enregistrez votre projet, toutes les
  //   informations du tracker seront
  //   définitivement effacées.
endmodule

module UART (
  input  A,
  output [7:0] D,
  output [2:0] S_COUNT
);

  wire and_1_out, CLK_out, count_8bits_1_max, not_1_out, s_r_ff_1_q, s_r_ff_2_q, xnor_1_out;
  wire [1:0] count_4bits_1_d;
  wire [1:1] multiplexer_1_out;
  wire [7:0] bit_extender_1_out;

  not not_1 (not_1_out, A);
  S_R_Flip_Flop s_r_ff_1 (.S(not_1_out), .R(1'b0), .clk(and_1_out), .Q(s_r_ff_1_q));  // open: reset, Qn, preset
  assign bit_extender_1_out = {{7{A}}, A};  // Bit_Extender bit_extender_1
  Clock CLK (.out(CLK_out));
  COUNT_4BITS count_4bits_1 (.A(1'b1), .CLK(CLK_out), .D(count_4bits_1_d));  // open: MAX
  COUNT_8BITS count_8bits_1 (.A(multiplexer_1_out[1]), .CLK(and_1_out), .C(S_COUNT), .MAX(count_8bits_1_max));
  S_R_Flip_Flop s_r_ff_2 (.S(count_8bits_1_max), .R(1'b0), .clk(and_1_out), .Q(s_r_ff_2_q));  // open: reset, Qn, preset
  and and_1 (and_1_out, count_4bits_1_d[0], count_4bits_1_d[1]);
  Multiplexer #(.enable("false")) multiplexer_1 (.in0(1'b1), .in1(1'b0), .out(multiplexer_1_out[1]), .sel(xnor_1_out));
  xnor xnor_1 (xnor_1_out, s_r_ff_1_q, s_r_ff_2_q);
  SHREGI_8BITS shregi_8bits_1 (
    .L(1'b0), .S({2{multiplexer_1_out[1]}}), .D(bit_extender_1_out), .R(A), .CLK(and_1_out), .Q(D));

  // Notes on the sheet:
  //   Attention, votre version de Logisim
  //   ne contient pas de tracker. Si vous
  //   enregistrez votre projet, toutes les
  //   informations du tracker seront
  //   définitivement effacées.
endmodule

module COUNT_4BITS (
  input  A,
  input  CLK,
  output [1:0] D,
  output MAX
);

  wire count_base_1_c;

  COUNT_BASE count_base_1 (.EN(A), .CLK(CLK), .Q(D[0]), .C(count_base_1_c));
  COUNT_BASE count_base_2 (.EN(count_base_1_c), .CLK(CLK), .Q(D[1]));  // open: C
  and and_1 (MAX, D[0], D[1]);

  // Notes on the sheet:
  //   Attention, votre version de Logisim
  //   ne contient pas de tracker. Si vous
  //   enregistrez votre projet, toutes les
  //   informations du tracker seront
  //   définitivement effacées.
endmodule

module COUNT_8BITS (
  input  A,
  input  CLK,
  output [2:0] C,
  output MAX
);

  wire count_base_1_c, count_base_2_c;

  COUNT_BASE count_base_1 (.EN(A), .CLK(CLK), .Q(C[0]), .C(count_base_1_c));
  COUNT_BASE count_base_2 (.EN(count_base_1_c), .CLK(CLK), .Q(C[1]), .C(count_base_2_c));
  COUNT_BASE count_base_3 (.EN(count_base_2_c), .CLK(CLK), .Q(C[2]));  // open: C
  and and_1 (MAX, C[0], C[1], C[2]);

  // Notes on the sheet:
  //   Attention, votre version de Logisim
  //   ne contient pas de tracker. Si vous
  //   enregistrez votre projet, toutes les
  //   informations du tracker seront
  //   définitivement effacées.
endmodule

module REGI_4BITS (
  input  [3:0] D,
  input  S,
  input  CLR,
  input  CLK,
  output [3:0] Q
);

  wire multiplexer_1_out, multiplexer_2_out, multiplexer_3_out, multiplexer_4_out;

  D_Flip_Flop d_ff_1 (.D(multiplexer_1_out), .clk(CLK), .Q(Q[3]), .reset(CLR));  // open: Qn, preset
  Multiplexer #(.enable("false")) multiplexer_1 (.in0(Q[3]), .in1(D[3]), .out(multiplexer_1_out), .sel(S));
  Multiplexer #(.enable("false")) multiplexer_2 (.in0(Q[2]), .in1(D[2]), .out(multiplexer_2_out), .sel(S));
  D_Flip_Flop d_ff_2 (.D(multiplexer_2_out), .clk(CLK), .Q(Q[2]), .reset(CLR));  // open: Qn, preset
  Multiplexer #(.enable("false")) multiplexer_3 (.in0(Q[1]), .in1(D[1]), .out(multiplexer_3_out), .sel(S));
  D_Flip_Flop d_ff_3 (.D(multiplexer_3_out), .clk(CLK), .Q(Q[1]), .reset(CLR));  // open: Qn, preset
  Multiplexer #(.enable("false")) multiplexer_4 (.in0(Q[0]), .in1(D[0]), .out(multiplexer_4_out), .sel(S));
  D_Flip_Flop d_ff_4 (.D(multiplexer_4_out), .clk(CLK), .Q(Q[0]), .reset(CLR));  // open: Qn, preset

  // Notes on the sheet:
  //   Attention, votre version de Logisim
  //   ne contient pas de tracker. Si vous
  //   enregistrez votre projet, toutes les
  //   informations du tracker seront
  //   définitivement effacées.
endmodule

module CHRONO_COUNT_4BITS (
  output [1:0] D
);

  wire CLK_out, counter_1_q;

  Counter #(.width(1), .max('h1)) counter_1 (
    .clr(1'b0), .load(1'b0), .up(1'b1), .count(1'b1), .clk(CLK_out), .Q(counter_1_q));  // open: D, carry
  Clock CLK (.out(CLK_out));
  Clock sysclk ();  // open: out
  COUNT_4BITS count_4bits_1 (.A(counter_1_q), .CLK(CLK_out), .D(D));  // open: MAX

  // Notes on the sheet:
  //   Attention, votre version de Logisim
  //   ne contient pas de tracker. Si vous
  //   enregistrez votre projet, toutes les
  //   informations du tracker seront
  //   définitivement effacées.
endmodule

module CHRONO_COUNT_8BITS (
  output [2:0] C,
  output MAX
);

  wire CLK_out, counter_1_q;

  Counter #(.width(1), .max('h1)) counter_1 (
    .clr(1'b0), .load(1'b0), .up(1'b1), .count(1'b1), .clk(CLK_out), .Q(counter_1_q));  // open: D, carry
  Clock CLK (.out(CLK_out));
  Clock sysclk ();  // open: out
  COUNT_8BITS count_8bits_1 (.A(counter_1_q), .CLK(CLK_out), .C(C), .MAX(MAX));

  // Notes on the sheet:
  //   Attention, votre version de Logisim
  //   ne contient pas de tracker. Si vous
  //   enregistrez votre projet, toutes les
  //   informations du tracker seront
  //   définitivement effacées.
endmodule

module CHRONO_SHREGI_8BITS (
  output [7:0] Q
);

  wire CLK_out;
  wire [7:0] counter_1_q;

  Counter counter_1 (
    .clr(1'b0), .load(1'b0), .up(1'b1), .count(1'b1), .clk(CLK_out), .Q(counter_1_q));  // open: D, carry
  Clock CLK (.out(CLK_out));
  Clock sysclk ();  // open: out
  SHREGI_8BITS shregi_8bits_1 (.L(1'b0), .S(2'b11), .D(counter_1_q), .R(1'b1), .CLK(CLK_out), .Q(Q));

  // Notes on the sheet:
  //   Attention, votre version de Logisim
  //   ne contient pas de tracker. Si vous
  //   enregistrez votre projet, toutes les
  //   informations du tracker seront
  //   définitivement effacées.
endmodule

module STATE_MACHINE (
  input  lastbit,
  input  count4bits,
  input  count8bit,
  output D
);

  wire not_1_out, s_r_ff_1_q, s_r_ff_2_q, xnor_1_out;

  not not_1 (not_1_out, lastbit);
  S_R_Flip_Flop s_r_ff_1 (.S(not_1_out), .R(1'b0), .clk(count4bits), .Q(s_r_ff_1_q));  // open: reset, Qn, preset
  S_R_Flip_Flop s_r_ff_2 (.S(count8bit), .R(1'b0), .clk(count4bits), .Q(s_r_ff_2_q));  // open: reset, Qn, preset
  Multiplexer #(.enable("false")) multiplexer_1 (.in0(1'b1), .in1(1'b0), .out(D), .sel(xnor_1_out));
  xnor xnor_1 (xnor_1_out, s_r_ff_1_q, s_r_ff_2_q);

  // Notes on the sheet:
  //   Attention, votre version de Logisim
  //   ne contient pas de tracker. Si vous
  //   enregistrez votre projet, toutes les
  //   informations du tracker seront
  //   définitivement effacées.
endmodule

module UART_V2 (
  input  A,
  output [7:0] D
);

  wire CLK_out, count_4bits_1_max, count_8bits_1_max;
  wire [1:1] state_machine_1_p4;
  wire [7:0] bit_extender_1_out;

  Clock CLK (.out(CLK_out));
  COUNT_4BITS count_4bits_1 (.A(1'b1), .CLK(CLK_out), .MAX(count_4bits_1_max));  // open: D
  assign bit_extender_1_out = {{7{A}}, A};  // Bit_Extender bit_extender_1
  COUNT_8BITS count_8bits_1 (.A(state_machine_1_p4[1]), .CLK(count_4bits_1_max), .MAX(count_8bits_1_max));  // open: C
  // STATE_MACHINE state_machine_1: pin names not known; wires that end beside it: A, count_8bits_1_max, count_4bits_1_max, state_machine_1_p4[1]
  SHREGI_8BITS shregi_8bits_1 (
    .L(1'b0), .S({2{state_machine_1_p4[1]}}), .D(bit_extender_1_out), .R(A), .CLK(count_4bits_1_max), .Q(D));

  // Notes on the sheet:
  //   Attention, votre version de Logisim
  //   ne contient pas de tracker. Si vous
  //   enregistrez votre projet, toutes les
  //   informations du tracker seront
  //   définitivement effacées.
endmodule
