// Logisim project Labo5_Melly_RouvinezV3.circ as structural Verilog: 14 circuits, main circuit UART
module COUNT_BASE (
  input  EN,
  input  CLK,
  input  CLR,
  output Q,
  output C
);

  wire xor_1_out;

  xor xor_1 (xor_1_out, Q, EN);
  and and_1 (C, Q, EN);
  D_Flip_Flop d_ff_1 (.D(xor_1_out), .clk(CLK), .Q(Q), .reset(CLR));  // open: Qn, preset

  // Notes on the sheet:
  //   Attention, votre version de Logisim
  //   ne contient pas de tracker. Si vous
  //   enregistrez votre projet, toutes les
  //   informations du tracker seront
  //   définitivement effacées.
endmodule

module SHREGI_8BITS (
  input  L,
  input  [1:0] S,
  input  [7:0] D,
  input  R,
  input  CLK,
  input  CLR,
  output [7:0] Q
);

  wire bitselector_1_out, bitselector_2_out;

  SHREGI_4BITS SHREGI_4BITS_1 (.D(D[3:0]), .R(bitselector_1_out), .L(L), .S(S), .CLK(CLK), .CLR(CLR), .Q(Q[3:0]));
  SHREGI_4BITS SHREGI_4BITS_2 (.D(D[7:4]), .R(R), .L(bitselector_2_out), .S(S), .CLK(CLK), .CLR(CLR), .Q(Q[7:4]));
  BitSelector #(.width(4)) bitselector_1 (.in(Q[7:4]), .out(bitselector_1_out), .sel(2'b00));
  BitSelector #(.width(4)) bitselector_2 (.in(Q[3:0]), .out(bitselector_2_out), .sel(2'b11));

  // Notes on the sheet:
  //   Attention, votre version de Logisim
  //   ne contient pas de tracker. Si vous
  //   enregistrez votre projet, toutes les
  //   informations du tracker seront
  //   définitivement effacées.
endmodule

module SHREGI_4BITS (
  input  [3:0] D,
  input  R,
  input  L,
  input  [1:0] S,
  input  CLK,
  input  CLR,
  output [3:0] Q
);

  wire multiplexer_1_out, multiplexer_2_out, multiplexer_3_out, multiplexer_4_out;

  Multiplexer #(.select(2), .enable("false")) multiplexer_1 (
    .in0(Q[3]), .in1(D[3]), .in2(Q[2]), .in3(R), .out(multiplexer_1_out), .sel(S));
  D_Flip_Flop d_ff_1 (.D(multiplexer_1_out), .clk(CLK), .Q(Q[3]), .reset(CLR));  // open: Qn, preset
  Multiplexer #(.select(2), .enable("false")) multiplexer_2 (
    .in0(Q[2]), .in1(D[2]), .in2(Q[1]), .in3(Q[3]), .out(multiplexer_2_out), .sel(S));
  D_Flip_Flop d_ff_2 (.D(multiplexer_2_out), .clk(CLK), .Q(Q[2]), .reset(CLR));  // open: Qn, preset
  Multiplexer #(.select(2), .enable("false")) multiplexer_3 (
    .in0(Q[1]), .in1(D[1]), .in2(Q[0]), .in3(Q[2]), .out(multiplexer_3_out), .sel(S));
  D_Flip_Flop d_ff_3 (.D(multiplexer_3_out), .clk(CLK), .Q(Q[1]), .reset(CLR));  // open: Qn, preset
  Multiplexer #(.select(2), .enable("false")) multiplexer_4 (
    .in0(Q[0]), .in1(D[0]), .in2(L), .in3(Q[1]), .out(multiplexer_4_out), .sel(S));
  D_Flip_Flop d_ff_4 (.D(multiplexer_4_out), .clk(CLK), .Q(Q[0]), .reset(CLR));  // open: Qn, preset

  // Notes on the sheet:
  //   Attention, votre version de Logisim
  //   ne contient pas de tracker. Si vous
  //   enregistrez votre projet, toutes les
  //   informations du tracker seront
  //   définitivement effacées.
endmodule

module COUNT_4BITS (
  input  A,
  input  CLR,
  input  CLK,
  output [1:0] D,
  output MAX
);

  wire COUNT_BASE_1_c;

  COUNT_BASE COUNT_BASE_1 (.EN(A), .CLK(CLK), .CLR(CLR), .Q(D[0]), .C(COUNT_BASE_1_c));
  COUNT_BASE COUNT_BASE_2 (.EN(COUNT_BASE_1_c), .CLK(CLK), .CLR(CLR), .Q(D[1]));  // open: C
  and and_1 (MAX, D[0], D[1]);

  // Notes on the sheet:
  //   Attention, votre version de Logisim
  //   ne contient pas de tracker. Si vous
  //   enregistrez votre projet, toutes les
  //   informations du tracker seront
  //   définitivement effacées.
endmodule

module COUNT_8BITS (
  input  A,
  input  CLR,
  input  CLK,
  output [2:0] C,
  output MAX
);

  wire COUNT_BASE_1_c, COUNT_BASE_2_c;

  COUNT_BASE COUNT_BASE_1 (.EN(A), .CLK(CLK), .CLR(CLR), .Q(C[0]), .C(COUNT_BASE_1_c));
  COUNT_BASE COUNT_BASE_2 (.EN(COUNT_BASE_1_c), .CLK(CLK), .CLR(CLR), .Q(C[1]), .C(COUNT_BASE_2_c));
  COUNT_BASE COUNT_BASE_3 (.EN(COUNT_BASE_2_c), .CLK(CLK), .CLR(CLR), .Q(C[2]));  // open: C
  and and_1 (MAX, C[0], C[1], C[2]);

  // Notes on the sheet:
  //   Attention, votre version de Logisim
  //   ne contient pas de tracker. Si vous
  //   enregistrez votre projet, toutes les
  //   informations du tracker seront
  //   définitivement effacées.
endmodule

module REGI_4BITS (
  input  [3:0] D,
  input  S,
  input  CLR,
  input  CLK,
  output [3:0] Q
);

  wire multiplexer_1_out, multiplexer_2_out, multiplexer_3_out, multiplexer_4_out;

  D_Flip_Flop d_ff_1 (.D(multiplexer_1_out), .clk(CLK), .Q(Q[3]), .reset(CLR));  // open: Qn, preset
  Multiplexer #(.enable("false")) multiplexer_1 (.in0(Q[3]), .in1(D[3]), .out(multiplexer_1_out), .sel(S));
  Multiplexer #(.enable("false")) multiplexer_2 (.in0(Q[2]), .in1(D[2]), .out(multiplexer_2_out), .sel(S));
  D_Flip_Flop d_ff_2 (.D(multiplexer_2_out), .clk(CLK), .Q(Q[2]), .reset(CLR));  // open: Qn, preset
  Multiplexer #(.enable("false")) multiplexer_3 (.in0(Q[1]), .in1(D[1]), .out(multiplexer_3_out), .sel(S));
  D_Flip_Flop d_ff_3 (.D(multiplexer_3_out), .clk(CLK), .Q(Q[1]), .reset(CLR));  // open: Qn, preset
  Multiplexer #(.enable("false")) multiplexer_4 (.in0(Q[0]), .in1(D[0]), .out(multiplexer_4_out), .sel(S));
  D_Flip_Flop d_ff_4 (.D(multiplexer_4_out), .clk(CLK), .Q(Q[0]), .reset(CLR));  // open: Qn, preset

  // Notes on the sheet:
  //   Attention, votre version de Logisim
  //   ne contient pas de tracker. Si vous
  //   enregistrez votre projet, toutes les
  //   informations du tracker seront
  //   définitivement effacées.
endmodule

module CHRONO_COUNT_4BITS (
  output [1:0] D,
  output MAX
);

  wire CLK_out;

  Counter #(.width(4), .max('hf)) counter_1 (
    .clr(1'b0), .load(1'b0), .up(1'b1), .count(1'b1), .clk(CLK_out));  // open: D, carry, Q
  Clock CLK (.out(CLK_out));
  Clock sysclk ();  // open: out
  COUNT_4BITS count_4bits_1 (.A(1'b1), .CLK(CLK_out), .D(D), .MAX(MAX));  // open: CLR

  // Notes on the sheet:
  //   Attention, votre version de Logisim
  //   ne contient pas de tracker. Si vous
  //   enregistrez votre projet, toutes les
  //   informations du tracker seront
  //   définitivement effacées.
endmodule

module CHRONO_COUNT_8BITS (
  output [2:0] D,
  output MAX
);

  wire CLK_out;

  Counter #(.width(3), .max('h7)) counter_1 (
    .clr(1'b0), .load(1'b0), .up(1'b1), .count(1'b1), .clk(CLK_out));  // open: D, carry, Q
  Clock CLK (.out(CLK_out));
  Clock sysclk ();  // open: out
  COUNT_8BITS count_8bits_1 (.A(1'b1), .CLK(CLK_out), .C(D), .MAX(MAX));  // open: CLR

  // Notes on the sheet:
  //   Attention, votre version de Logisim
  //   ne contient pas de tracker. Si vous
  //   enregistrez votre projet, toutes les
  //   informations du tracker seront
  //   définitivement effacées.
endmodule

module CHRONO_SHREGI_8BITS (
  input  [1:0] in_1,
  output [7:0] Q
);

  wire CLK_out;
  wire [7:0] counter_1_q;

  Counter counter_1 (
    .clr(1'b0), .load(1'b0), .up(1'b1), .count(1'b1), .clk(CLK_out), .Q(counter_1_q));  // open: D, carry
  Clock CLK (.out(CLK_out));
  Clock sysclk ();  // open: out
  SHREGI_8BITS shregi_8bits_1 (.L(1'b0), .S(in_1), .D(counter_1_q), .R(1'b1), .CLK(CLK_out), .Q(Q));  // open: CLR

  // Notes on the sheet:
  //   Attention, votre version de Logisim
  //   ne contient pas de tracker. Si vous
  //   enregistrez votre projet, toutes les
  //   informations du tracker seront
  //   définitivement effacées.
endmodule

module STAMAC (
  input  START_BIT,
  input  COUNT_8BITS_MAX,
  input  COUNT_4BITS_MAX,
  input  CLR,
  input  CLK,
  output D
);

  wire and_1_out, and_2_out, s_r_ff_1_q, s_r_ff_2_q, xor_1_out;

  and and_1 (and_1_out, COUNT_4BITS_MAX, COUNT_8BITS_MAX);
  and and_2 (and_2_out, COUNT_4BITS_MAX, START_BIT);
  S_R_Flip_Flop #(.trigger("falling")) s_r_ff_1 (
    .S(and_2_out), .R(1'b0), .clk(CLK), .Q(s_r_ff_1_q), .reset(CLR));  // open: Qn, preset
  S_R_Flip_Flop #(.trigger("falling")) s_r_ff_2 (
    .S(and_1_out), .R(1'b0), .clk(CLK), .Q(s_r_ff_2_q), .reset(CLR));  // open: Qn, preset
  xor xor_1 (xor_1_out, s_r_ff_1_q, s_r_ff_2_q);
  Multiplexer #(.enable("false")) multiplexer_1 (.in0(1'b0), .in1(xor_1_out), .out(D), .sel(COUNT_4BITS_MAX));

  // Notes on the sheet:
  //   Attention, votre version de Logisim
  //   ne contient pas de tracker. Si vous
  //   enregistrez votre projet, toutes les
  //   informations du tracker seront
  //   définitivement effacées.
endmodule

module UART (
  input  A,
  input  CLR,
  output [7:0] out_3,
  output [7:0] D
);

  wire COUNT_4BITS_1_max, COUNT_8BITS_1_max, start_bit_1_start, sysclk_out;
  wire [1:0] COUNT_4BITS_1_d;
  wire [1:1] STAMAC_1_d;
  wire [7:0] bit_extender_1_out;

  Clock sysclk (.out(sysclk_out));
  COUNT_4BITS COUNT_4BITS_1 (.A(1'b1), .CLR(CLR), .CLK(sysclk_out), .D(COUNT_4BITS_1_d), .MAX(COUNT_4BITS_1_max));
  assign bit_extender_1_out = {{7{A}}, A};  // Bit_Extender bit_extender_1
  START_BIT start_bit_1 (.CPT4(COUNT_4BITS_1_d), .A(A), .CLR(CLR), .CLK(sysclk_out), .START(start_bit_1_start));
  COUNT_8BITS COUNT_8BITS_1 (.A(STAMAC_1_d[1]), .CLR(CLR), .CLK(sysclk_out), .MAX(COUNT_8BITS_1_max));  // open: C
  STAMAC STAMAC_1 (
    .START_BIT(start_bit_1_start), .COUNT_8BITS_MAX(COUNT_8BITS_1_max), .COUNT_4BITS_MAX(COUNT_4BITS_1_max),
    .CLR(CLR), .CLK(sysclk_out), .D(STAMAC_1_d[1]));
  SHREGI_8BITS SHREGI_8BITS_1 (
    .L(1'b0), .S({2{STAMAC_1_d[1]}}), .D(bit_extender_1_out), .R(A), .CLK(sysclk_out), .CLR(CLR), .Q(out_3));
  REGI_8BITS REGI_8BITS_1 (.S(COUNT_8BITS_1_max), .A(out_3), .CLR(CLR), .CLK(sysclk_out), .Q(D));

  // Notes on the sheet:
  //   Attention, votre version de Logisim
  //   ne contient pas de tracker. Si vous
  //   enregistrez votre projet, toutes les
  //   informations du tracker seront
  //   définitivement effacées.
endmodule

module REGI_8BITS (
  input  S,
  input  [7:0] A,
  input  CLR,
  input  CLK,
  output [7:0] Q
);

  REGI_4BITS REGI_4BITS_1 (.D(A[3:0]), .S(S), .CLR(CLR), .CLK(CLK), .Q(Q[3:0]));
  REGI_4BITS REGI_4BITS_2 (.D(A[7:4]), .S(S), .CLR(CLR), .CLK(CLK), .Q(Q[7:4]));

  // Notes on the sheet:
  //   Attention, votre version de Logisim
  //   ne contient pas de tracker. Si vous
  //   enregistrez votre projet, toutes les
  //   informations du tracker seront
  //   définitivement effacées.
endmodule

module START_BIT (
  input  [1:0] CPT4,
  input  A,
  input  CLR,
  input  CLK,
  output START
);

  wire and_1_out, and_2_out, and_3_out, nor_1_out, not_1_out, not_2_out, s_r_ff_1_q, s_r_ff_2_q;

  not not_1 (not_1_out, CPT4[1]);
  nor nor_1 (nor_1_out, CPT4[0], CPT4[1]);
  not not_2 (not_2_out, A);
  and and_1 (and_1_out, not_1_out, A);
  S_R_Flip_Flop s_r_ff_1 (.S(and_1_out), .R(1'b0), .clk(CLK), .Q(s_r_ff_1_q), .reset(nor_1_out));  // open: Qn, preset
  and and_2 (and_2_out, not_2_out, CPT4[1]);
  S_R_Flip_Flop s_r_ff_2 (.S(and_2_out), .R(1'b0), .clk(CLK), .Q(s_r_ff_2_q), .reset(nor_1_out));  // open: Qn, preset
  and and_3 (and_3_out, s_r_ff_1_q, s_r_ff_2_q);
  S_R_Flip_Flop s_r_ff_3 (.S(and_3_out), .R(1'b0), .clk(CLK), .Q(START), .reset(CLR));  // open: Qn, preset

  // Notes on the sheet:
  //   Attention, votre version de Logisim
  //   ne contient pas de tracker. Si vous
  //   enregistrez votre projet, toutes les
  //   informations du tracker seront
  //   définitivement effacées.
endmodule

module oldstart (
);

  wire and_1_out, and_2_out, and_3_out, E2_out, nor_1_out, not_1_out, not_2_out, s_r_ff_1_q, s_r_ff_2_q,
       undriven, undriven_2, undriven_3, undriven_4, undriven_5;

  not not_1 (not_1_out, undriven);
  and E2 (E2_out, undriven_2, not_1_out);
  nor nor_1 (nor_1_out, undriven_2, undriven);
  and and_1 (and_1_out, undriven_5, E2_out);
  and and_2 (and_2_out, undriven_5, undriven_4);
  S_R_Flip_Flop s_r_ff_1 (
    .S(undriven_3), .R(1'b0), .clk(and_1_out), .Q(s_r_ff_1_q), .reset(nor_1_out));  // open: Qn, preset
  not not_2 (not_2_out, undriven_3);
  S_R_Flip_Flop s_r_ff_2 (
    .S(not_2_out), .R(1'b0), .clk(and_2_out), .Q(s_r_ff_2_q), .reset(nor_1_out));  // open: Qn, preset
  and and_3 (and_3_out, s_r_ff_1_q, s_r_ff_2_q);
  S_R_Flip_Flop s_r_ff_3 (.S(and_3_out), .R(1'b0), .clk(undriven_5));  // open: Q, reset, Qn, preset

  // Notes on the sheet:
  //   Attention, votre version de Logisim
  //   ne contient pas de tracker. Si vous
  //   enregistrez votre projet, toutes les
  //   informations du tracker seront
  //   définitivement effacées.
endmodule
