// Logisim project emetteur.circ as structural Verilog: 30 circuits, main circuit LatchD
module LatchD (
  input  D,
  input  LD,
  output Q,
  output Q2
);

  wire and_1_out, and_2_out, not_1_out;

  not not_1 (not_1_out, D);
  and and_1 (and_1_out, not_1_out, LD);
  and and_2 (and_2_out, LD, D);
  nor nor_1 (Q, and_1_out, Q2);
  nor nor_2 (Q2, Q, and_2_out);

  // Notes on the sheet:
  //   Attention, votre version de Logisim
  //   ne contient pas de tracker. Si vous
  //   enregistrez votre projet, toutes les
  //   informations du tracker seront
  //   définitivement effacées.
endmodule

module FlipFlop (
  input  D,
  input  CK,
  output Q,
  output Q2
);

  wire Maitre_q, not_1_out, not_2_out;

  not not_1 (not_1_out, CK);
  LatchD Maitre (.D(D), .LD(not_1_out), .Q(Maitre_q));  // open: Q2
  not not_2 (not_2_out, not_1_out);
  LatchD latchd_1 (.D(Maitre_q), .LD(not_2_out), .Q(Q), .Q2(Q2));

  // Notes on the sheet:
  //   Attention, votre version de Logisim
  //   ne contient pas de tracker. Si vous
  //   enregistrez votre projet, toutes les
  //   informations du tracker seront
  //   définitivement effacées.
endmodule

module LFSR4bits (
  input  in_1,
  input  in_2,
  input  in_3,
  input  in_4,
  input  in_5,
  input  [1:0] in_6,
  input  in_7,
  output out_8,
  output out_9
);

  wire d_ff_3_q, d_ff_4_q, multiplexer_1_out, multiplexer_2_out, multiplexer_3_out, multiplexer_4_out,
       xor_1_out;

  Multiplexer #(.select(2), .enable("false")) multiplexer_1 (
    .in0(out_8), .in1(out_9), .in2(in_1), .in3(xor_1_out), .out(multiplexer_1_out), .sel(in_6));
  D_Flip_Flop d_ff_1 (.D(multiplexer_1_out), .clk(in_7), .Q(out_8));  // open: Qn, preset, reset
  Multiplexer #(.select(2), .enable("false")) multiplexer_2 (
    .in0(out_9), .in1(d_ff_3_q), .in2(in_2), .in3(out_8), .out(multiplexer_2_out), .sel(in_6));
  D_Flip_Flop d_ff_2 (.D(multiplexer_2_out), .clk(in_7), .Q(out_9));  // open: Qn, preset, reset
  Multiplexer #(.select(2), .enable("false")) multiplexer_3 (
    .in0(d_ff_3_q), .in1(d_ff_4_q), .in2(in_3), .in3(out_9), .out(multiplexer_3_out), .sel(in_6));
  xor xor_1 (xor_1_out, d_ff_3_q, d_ff_4_q);
  D_Flip_Flop d_ff_3 (.D(multiplexer_3_out), .clk(in_7), .Q(d_ff_3_q));  // open: Qn, preset, reset
  Multiplexer #(.select(2), .enable("false")) multiplexer_4 (
    .in0(d_ff_4_q), .in1(in_5), .in2(in_4), .in3(d_ff_3_q), .out(multiplexer_4_out), .sel(in_6));
  D_Flip_Flop d_ff_4 (.D(multiplexer_4_out), .clk(in_7), .Q(d_ff_4_q));  // open: Qn, preset, reset

  // Other names for the same wires on the sheet: S[1:0] = in_6

  // Notes on the sheet:
  //   Attention, votre version de Logisim
  //   ne contient pas de tracker. Si vous
  //   enregistrez votre projet, toutes les
  //   informations du tracker seront
  //   définitivement effacées.
endmodule

module Compteur03 (
  input  count,
  input  Reset,
  output [1:0] CPT3_val,
  output Done3
);

  wire and_1_out, CK, xor_1_out, xor_2_out;

  Clock u_CK (.out(CK));
  xor xor_1 (xor_1_out, CPT3_val[0], count);
  and and_1 (and_1_out, CPT3_val[0], count);
  xor xor_2 (xor_2_out, CPT3_val[1], and_1_out);
  D_Flip_Flop d_ff_1 (.D(xor_1_out), .clk(CK), .Q(CPT3_val[0]), .reset(Reset));  // open: Qn, preset
  D_Flip_Flop d_ff_2 (.D(xor_2_out), .clk(CK), .Q(CPT3_val[1]), .reset(Reset));  // open: Qn, preset
  and and_2 (Done3, CPT3_val[0], CPT3_val[1]);

  // Notes on the sheet:
  //   Attention, votre version de Logisim
  //   ne contient pas de tracker. Si vous
  //   enregistrez votre projet, toutes les
  //   informations du tracker seront
  //   définitivement effacées.
endmodule

module CPT3_normal (
  input  count3,
  output [1:0] comptage3,
  output done3
);

  wire and_1_out, and_2_out, CK, not_1_out, xor_1_out;

  Clock sysclk (.out(CK));
  not not_1 (not_1_out, comptage3[0]);
  and and_1 (and_1_out, not_1_out, count3);
  xor xor_1 (xor_1_out, comptage3[1], comptage3[0]);
  and and_2 (and_2_out, xor_1_out, count3);
  D_Flip_Flop d_ff_1 (.D(and_1_out), .clk(CK), .Q(comptage3[0]));  // open: Qn, preset, reset
  D_Flip_Flop d_ff_2 (.D(and_2_out), .clk(CK), .Q(comptage3[1]));  // open: Qn, preset, reset
  and and_3 (done3, comptage3[0], comptage3[1]);

  // Notes on the sheet:
  //   Attention, votre version de Logisim
  //   ne contient pas de tracker. Si vous
  //   enregistrez votre projet, toutes les
  //   informations du tracker seront
  //   définitivement effacées.
endmodule

module CPT71 (
  input  in_1,
  input  clk,
  output [2:0] out_3,
  output out_4
);

  wire and_1_out, and_2_out, and_3_out, and_4_out, and_5_out, not_1_out, not_2_out, or_1_out, xor_1_out,
       xor_2_out;

  not not_1 (not_1_out, out_3[0]);
  xor xor_1 (xor_1_out, out_3[1], out_3[0]);
  xor xor_2 (xor_2_out, out_3[2], out_3[0]);
  not not_2 (not_2_out, out_3[1]);
  and and_1 (and_1_out, not_2_out, out_3[2]);
  and and_2 (and_2_out, not_1_out, in_1);
  and and_3 (and_3_out, xor_1_out, in_1);
  and and_4 (and_4_out, xor_2_out, out_3[1]);
  D_Flip_Flop d_ff_1 (.D(and_2_out), .clk(clk), .Q(out_3[0]));  // open: Qn, preset, reset
  D_Flip_Flop d_ff_2 (.D(and_3_out), .clk(clk), .Q(out_3[1]));  // open: Qn, preset, reset
  D_Flip_Flop d_ff_3 (.D(and_5_out), .clk(clk), .Q(out_3[2]));  // open: Qn, preset, reset
  or or_1 (or_1_out, and_4_out, and_1_out);
  and and_5 (and_5_out, or_1_out, in_1);
  and and_6 (out_4, out_3[0], out_3[1], out_3[2]);

  // Other names for the same wires on the sheet: CK = clk

  // Notes on the sheet:
  //   Attention, votre version de Logisim
  //   ne contient pas de tracker. Si vous
  //   enregistrez votre projet, toutes les
  //   informations du tracker seront
  //   définitivement effacées.
endmodule

module CPT7_RS (
  input  in_1,
  output [2:0] out_2,
  output out_3
);

  wire CK, undriven, undriven_2, xor_1_out;

  Clock clock_1 (.out(CK));
  xor xor_1 (xor_1_out, out_2[0], in_1);
  D_Flip_Flop d_ff_1 (.D(xor_1_out), .clk(CK), .Q(out_2[0]));  // open: Qn, preset, reset
  D_Flip_Flop d_ff_2 (.D(undriven), .clk(CK), .Q(out_2[1]));  // open: Qn, preset, reset
  D_Flip_Flop d_ff_3 (.D(undriven_2), .clk(CK), .Q(out_2[2]));  // open: Qn, preset, reset
  and and_1 (out_3, out_2[0], out_2[1], out_2[2]);

  // Notes on the sheet:
  //   Attention, votre version de Logisim
  //   ne contient pas de tracker. Si vous
  //   enregistrez votre projet, toutes les
  //   informations du tracker seront
  //   définitivement effacées.
endmodule

module FSM1 (
  input  T2,
  input  T1,
  input  T0,
  input  U1,
  input  U0,
  input  V0,
  input  clk,
  output CPT7,
  output CPT3,
  output SEND
);

  wire a, and_1_out, and_2_out, and_3_out, and_4_out, b, c, nand_1_out, nand_2_out, or_1_out, or_2_out,
       or_3_out;

  and and_1 (and_1_out, CPT7, T2, T1, T0);
  or or_1 (or_1_out, ~V0, and_1_out);  // OR_Gate
  D_Flip_Flop d_ff_1 (.D(or_1_out), .clk(clk), .Q(a));  // open: Qn, preset, reset
  and and_2 (and_2_out, V0, a);
  D_Flip_Flop d_ff_2 (.D(and_2_out), .clk(clk), .Q(b));  // open: Qn, preset, reset
  nand nand_1 (nand_1_out, T2, T1, T0);
  and and_3 (and_3_out, nand_1_out, CPT7);
  D_Flip_Flop d_ff_3 (.D(or_2_out), .clk(clk), .Q(c));  // open: Qn, preset, reset
  or or_2 (or_2_out, and_3_out, b);
  nand nand_2 (nand_2_out, U0, U1, CPT3);
  D_Flip_Flop d_ff_4 (.D(or_3_out), .clk(clk), .Q(CPT3));  // open: Qn, preset, reset
  or or_3 (or_3_out, nand_2_out, c);
  D_Flip_Flop d_ff_5 (.D(and_4_out), .clk(clk), .Q(CPT7));  // open: Qn, preset, reset
  and and_4 (and_4_out, U0, U1, CPT3);

  assign SEND = CPT3;

  // Other names for the same wires on the sheet: CK = clk; d = CPT3; e = CPT7

  // Notes on the sheet:
  //   Attention, votre version de Logisim
  //   ne contient pas de tracker. Si vous
  //   enregistrez votre projet, toutes les
  //   informations du tracker seront
  //   définitivement effacées.
endmodule

module UART1 (
  input  in_1,
  output out_2
);

  wire clock_1_out, cpt3_1_done3, cpt71_1_out_4, fsm1_1_cpt3, fsm1_1_cpt7;
  wire [1:0] cpt3_1_cpt3_val;
  wire [2:0] cpt71_1_out_3;

  Clock clock_1 (.out(clock_1_out));
  CPT71 cpt71_1 (.in_1(fsm1_1_cpt7), .clk(clock_1_out), .out_3(cpt71_1_out_3), .out_4(cpt71_1_out_4));
  CPT3 cpt3_1 (.clk(clock_1_out), .CPT3_val(cpt3_1_cpt3_val), .Done3(cpt3_1_done3));  // open: count3
  FSM1 fsm1_1 (
    .T2(cpt71_1_out_3[2]), .T1(cpt71_1_out_3[1]), .T0(cpt71_1_out_3[0]), .U1(cpt3_1_cpt3_val[1]),
    .U0(cpt3_1_cpt3_val[0]), .V0(in_1), .clk(clock_1_out), .CPT7(fsm1_1_cpt7), .CPT3(fsm1_1_cpt3),
    .SEND(out_2));

  // Notes on the sheet:
  //   Attention, votre version de Logisim
  //   ne contient pas de tracker. Si vous
  //   enregistrez votre projet, toutes les
  //   informations du tracker seront
  //   définitivement effacées.
endmodule

module ShiftRegistre4bits (
  input  D3,
  input  D2,
  input  D1,
  input  D0,
  input  L,
  input  R,
  input  [1:0] S,
  input  clk,
  output Q3,
  output Q2,
  output Q1,
  output Q0
);

  wire multiplexer_1_out, multiplexer_2_out, multiplexer_3_out, multiplexer_4_out;

  Multiplexer #(.select(2), .enable("false")) multiplexer_1 (
    .in0(Q3), .in1(D3), .in2(Q2), .in3(R), .out(multiplexer_1_out), .sel(S));
  D_Flip_Flop d_ff_1 (.D(multiplexer_1_out), .clk(clk), .Q(Q3));  // open: Qn, preset, reset
  Multiplexer #(.select(2), .enable("false")) multiplexer_2 (
    .in0(Q2), .in1(D2), .in2(Q1), .in3(Q3), .out(multiplexer_2_out), .sel(S));
  D_Flip_Flop d_ff_2 (.D(multiplexer_2_out), .clk(clk), .Q(Q2));  // open: Qn, preset, reset
  Multiplexer #(.select(2), .enable("false")) multiplexer_3 (
    .in0(Q1), .in1(D1), .in2(Q0), .in3(Q2), .out(multiplexer_3_out), .sel(S));
  D_Flip_Flop d_ff_3 (.D(multiplexer_3_out), .clk(clk), .Q(Q1));  // open: Qn, preset, reset
  Multiplexer #(.select(2), .enable("false")) multiplexer_4 (
    .in0(Q0), .in1(D0), .in2(L), .in3(Q1), .out(multiplexer_4_out), .sel(S));
  D_Flip_Flop d_ff_4 (.D(multiplexer_4_out), .clk(clk), .Q(Q0));  // open: Qn, preset, reset

  // Notes on the sheet:
  //   Attention, votre version de Logisim
  //   ne contient pas de tracker. Si vous
  //   enregistrez votre projet, toutes les
  //   informations du tracker seront
  //   définitivement effacées.
endmodule

module ShiftRegistre8bits (
  input  [1:0] S,
  input  L,
  input  R,
  input  [7:0] Inflow,
  input  clk,
  output BIT_OUT,
  output [7:0] Outflow
);

  ShiftRegistre4bits SR_1 (
    .D3(Inflow[3]), .D2(Inflow[2]), .D1(Inflow[1]), .D0(Inflow[0]), .L(L), .R(Outflow[4]), .S(S), .clk(clk),
    .Q3(Outflow[3]), .Q2(Outflow[2]), .Q1(Outflow[1]), .Q0(BIT_OUT));
  ShiftRegistre4bits SR_2 (
    .D3(Inflow[7]), .D2(Inflow[6]), .D1(Inflow[5]), .D0(Inflow[4]), .L(Outflow[3]), .R(R), .S(S), .clk(clk),
    .Q3(Outflow[7]), .Q2(Outflow[6]), .Q1(Outflow[5]), .Q0(Outflow[4]));

  assign Outflow[0] = BIT_OUT;

  // Other names for the same wires on the sheet: CK = clk

  // Notes on the sheet:
  //   Attention, votre version de Logisim
  //   ne contient pas de tracker. Si vous
  //   enregistrez votre projet, toutes les
  //   informations du tracker seront
  //   définitivement effacées.
endmodule

module CPT3 (
  input  count3,
  input  clk,
  output [1:0] CPT3_val,
  output Done3
);

  wire and_1_out, and_2_out, not_1_out, not_2_out, xor_1_out;

  not not_1 (not_1_out, CPT3_val[0]);
  and and_1 (and_1_out, not_1_out, count3);
  xor xor_1 (xor_1_out, CPT3_val[1], CPT3_val[0]);
  and and_2 (and_2_out, xor_1_out, count3);
  D_Flip_Flop d_ff_1 (.D(and_1_out), .clk(clk), .Q(CPT3_val[0]));  // open: Qn, preset, reset
  D_Flip_Flop d_ff_2 (.D(and_2_out), .clk(clk), .Q(CPT3_val[1]));  // open: Qn, preset, reset
  not not_2 (not_2_out, CPT3_val[0]);
  and and_3 (Done3, not_2_out, CPT3_val[1]);

  // Other names for the same wires on the sheet: CK = clk

  // Notes on the sheet:
  //   Attention, votre version de Logisim
  //   ne contient pas de tracker. Si vous
  //   enregistrez votre projet, toutes les
  //   informations du tracker seront
  //   définitivement effacées.
endmodule

module CPT7 (
  input  count7,
  input  Reset,
  input  clk,
  output [2:0] CPT7_val,
  output Done7
);

  wire and_1_out, and_2_out, xor_1_out, xor_2_out, xor_3_out;

  and and_1 (and_1_out, CPT7_val[0], count7);
  and and_2 (and_2_out, CPT7_val[1], and_1_out);
  xor xor_1 (xor_1_out, CPT7_val[0], count7);
  xor xor_2 (xor_2_out, CPT7_val[1], and_1_out);
  xor xor_3 (xor_3_out, CPT7_val[2], and_2_out);
  D_Flip_Flop d_ff_1 (.D(xor_1_out), .clk(clk), .Q(CPT7_val[0]), .reset(Reset));  // open: Qn, preset
  D_Flip_Flop d_ff_2 (.D(xor_2_out), .clk(clk), .Q(CPT7_val[1]), .reset(Reset));  // open: Qn, preset
  D_Flip_Flop d_ff_3 (.D(xor_3_out), .clk(clk), .Q(CPT7_val[2]), .reset(Reset));  // open: Qn, preset
  and and_3 (Done7, CPT7_val[0], CPT7_val[1], CPT7_val[2]);

  // Other names for the same wires on the sheet: CK = clk

  // Notes on the sheet:
  //   Attention, votre version de Logisim
  //   ne contient pas de tracker. Si vous
  //   enregistrez votre projet, toutes les
  //   informations du tracker seront
  //   définitivement effacées.
endmodule

module FSM (
  input  CPT3,
  input  CPT7,
  input  SEND,
  input  Reset,
  input  clk,
  output Q0_out,
  output [1:0] SR,
  output [1:0] CPT3_C,
  output [1:0] CPT7_C,
  output LED
);

  wire and_1_out, and_2_out, and_3_out, and_4_out, and_5_out, and_6_out, and_7_out, and_8_out, not_1_out,
       not_2_out, not_3_out, not_4_out, not_5_out, not_6_out, not_7_out, not_8_out, or_1_out, or_2_out, Q1_q;

  not not_1 (not_1_out, CPT7);
  and and_1 (and_1_out, not_1_out, CPT7_C[1]);
  not not_2 (not_2_out, CPT3);
  and and_2 (and_2_out, not_2_out, CPT3_C[1]);
  not not_3 (not_3_out, CPT7_C[1]);
  not not_4 (not_4_out, CPT3_C[1]);
  and and_3 (and_3_out, CPT7_C[1], CPT7);
  not not_5 (not_5_out, SEND);
  and and_4 (and_4_out, not_5_out, not_4_out, not_3_out, not_6_out);
  D_Flip_Flop Q0 (.D(or_1_out), .clk(clk), .Q(Q0_out), .reset(Reset));  // open: Qn, preset
  or or_1 (or_1_out, and_3_out, and_4_out);
  not not_6 (not_6_out, Q1_q);
  D_Flip_Flop Q1 (.D(and_5_out), .clk(clk), .Q(Q1_q), .reset(Reset));  // open: Qn, preset
  and and_5 (and_5_out, Q0_out, SEND);
  D_Flip_Flop Q2 (.D(or_2_out), .clk(clk), .Q(CPT3_C[1]), .reset(Reset));  // open: Qn, preset
  or or_2 (or_2_out, Q1_q, and_1_out, and_2_out);
  D_Flip_Flop Q3 (.D(and_6_out), .clk(clk), .Q(CPT7_C[1]), .reset(Reset));  // open: Qn, preset
  and and_6 (and_6_out, CPT3_C[1], CPT3);
  not not_7 (not_7_out, CPT7_C[1]);
  not not_8 (not_8_out, CPT7_C[1]);
  and and_7 (and_7_out, Q1_q, not_7_out);
  and and_8 (and_8_out, Reset, not_8_out);
  or or_3 (SR[0], and_7_out, CPT7_C[1]);
  not not_9 (CPT3_C[0], CPT3_C[1]);
  or or_4 (CPT7_C[0], Q0_out, and_8_out);
  and and_9 (LED, CPT7, CPT7_C[1]);

  assign SR[1] = CPT7_C[1];

  // Other names for the same wires on the sheet: CK = clk; Q3 = CPT7_C[1]

  // Notes on the sheet:
  //   Attention, votre version de Logisim
  //   ne contient pas de tracker. Si vous
  //   enregistrez votre projet, toutes les
  //   informations du tracker seront
  //   définitivement effacées.
endmodule

module SIM (
  input  SEND,
  input  RST,
  input  [7:0] ENTRY,
  output [1:0] CPT3_VAL,
  output [1:0] SENDOUT,
  output [2:0] CPT7_VAL,
  output LED,
  output [7:0] out_8,
  output [7:0] out_9,
  output [7:0] SHIFT_OUT
);

  wire and_1_out, and_2_out, CK, cpt3_1_done3, cpt7_1_done7, fsm_1_q0_out, not_1_out, not_2_out, or_1_out,
       shiftregistre8bits_1_bit_out;
  wire [1:0] fsm_1_cpt3_c, fsm_1_cpt7_c;

  Clock sysclk (.out(CK));
  FSM fsm_1 (
    .CPT3(cpt3_1_done3), .CPT7(cpt7_1_done7), .SEND(SEND), .Reset(RST), .clk(CK), .Q0_out(fsm_1_q0_out),
    .SR(SENDOUT), .CPT3_C(fsm_1_cpt3_c), .CPT7_C(fsm_1_cpt7_c), .LED(LED));
  not not_1 (not_1_out, SENDOUT[1]);
  ShiftRegistre8bits shiftregistre8bits_1 (
    .S(SENDOUT), .L(1'b0), .R(1'b0), .Inflow(ENTRY), .clk(CK), .BIT_OUT(shiftregistre8bits_1_bit_out),
    .Outflow(SHIFT_OUT));
  CPT3 cpt3_1 (.count3(fsm_1_cpt3_c[1]), .clk(CK), .CPT3_val(CPT3_VAL), .Done3(cpt3_1_done3));
  CPT7 cpt7_1 (.count7(fsm_1_cpt7_c[1]), .Reset(fsm_1_cpt7_c[0]), .clk(CK), .CPT7_val(CPT7_VAL), .Done7(cpt7_1_done7));
  not not_2 (not_2_out, and_1_out);
  and and_1 (and_1_out, SENDOUT[0], not_1_out);
  and and_2 (and_2_out, fsm_1_q0_out, not_2_out);
  or or_1 (or_1_out, and_2_out, shiftregistre8bits_1_bit_out);
  UART uart_1 (.A(or_1_out), .CLR(RST), .out_3(out_8), .D(out_9));

  // Notes on the sheet:
  //   Attention, votre version de Logisim
  //   ne contient pas de tracker. Si vous
  //   enregistrez votre projet, toutes les
  //   informations du tracker seront
  //   définitivement effacées.
endmodule

module screens (
);

  ShiftRegistre8bits shiftregistre8bits_1 ();  // open: S, L, R, Inflow, clk, BIT_OUT, Outflow

  // Notes on the sheet:
  //   Attention, votre version de Logisim
  //   ne contient pas de tracker. Si vous
  //   enregistrez votre projet, toutes les
  //   informations du tracker seront
  //   définitivement effacées.
endmodule

module COUNT_BASE (
  input  EN,
  input  CLK,
  input  CLR,
  output Q,
  output C
);

  wire xor_1_out;

  xor xor_1 (xor_1_out, Q, EN);
  and and_1 (C, Q, EN);
  D_Flip_Flop d_ff_1 (.D(xor_1_out), .clk(CLK), .Q(Q), .reset(CLR));  // open: Qn, preset

  // Notes on the sheet:
  //   Attention, votre version de Logisim
  //   ne contient pas de tracker. Si vous
  //   enregistrez votre projet, toutes les
  //   informations du tracker seront
  //   définitivement effacées.
endmodule

module SHREGI_8BITS (
  input  L,
  input  [1:0] S,
  input  [7:0] D,
  input  R,
  input  CLK,
  input  CLR,
  output [7:0] Q
);

  wire bitselector_1_out, bitselector_2_out;

  SHREGI_4BITS SHREGI_4BITS_1 (.D(D[3:0]), .R(bitselector_1_out), .L(L), .S(S), .CLK(CLK), .CLR(CLR), .Q(Q[3:0]));
  SHREGI_4BITS SHREGI_4BITS_2 (.D(D[7:4]), .R(R), .L(bitselector_2_out), .S(S), .CLK(CLK), .CLR(CLR), .Q(Q[7:4]));
  BitSelector #(.width(4)) bitselector_1 (.in(Q[7:4]), .out(bitselector_1_out), .sel(2'b00));
  BitSelector #(.width(4)) bitselector_2 (.in(Q[3:0]), .out(bitselector_2_out), .sel(2'b11));

  // Notes on the sheet:
  //   Attention, votre version de Logisim
  //   ne contient pas de tracker. Si vous
  //   enregistrez votre projet, toutes les
  //   informations du tracker seront
  //   définitivement effacées.
endmodule

module SHREGI_4BITS (
  input  [3:0] D,
  input  R,
  input  L,
  input  [1:0] S,
  input  CLK,
  input  CLR,
  output [3:0] Q
);

  wire multiplexer_1_out, multiplexer_2_out, multiplexer_3_out, multiplexer_4_out;

  Multiplexer #(.select(2), .enable("false")) multiplexer_1 (
    .in0(Q[3]), .in1(D[3]), .in2(Q[2]), .in3(R), .out(multiplexer_1_out), .sel(S));
  D_Flip_Flop d_ff_1 (.D(multiplexer_1_out), .clk(CLK), .Q(Q[3]), .reset(CLR));  // open: Qn, preset
  Multiplexer #(.select(2), .enable("false")) multiplexer_2 (
    .in0(Q[2]), .in1(D[2]), .in2(Q[1]), .in3(Q[3]), .out(multiplexer_2_out), .sel(S));
  D_Flip_Flop d_ff_2 (.D(multiplexer_2_out), .clk(CLK), .Q(Q[2]), .reset(CLR));  // open: Qn, preset
  Multiplexer #(.select(2), .enable("false")) multiplexer_3 (
    .in0(Q[1]), .in1(D[1]), .in2(Q[0]), .in3(Q[2]), .out(multiplexer_3_out), .sel(S));
  D_Flip_Flop d_ff_3 (.D(multiplexer_3_out), .clk(CLK), .Q(Q[1]), .reset(CLR));  // open: Qn, preset
  Multiplexer #(.select(2), .enable("false")) multiplexer_4 (
    .in0(Q[0]), .in1(D[0]), .in2(L), .in3(Q[1]), .out(multiplexer_4_out), .sel(S));
  D_Flip_Flop d_ff_4 (.D(multiplexer_4_out), .clk(CLK), .Q(Q[0]), .reset(CLR));  // open: Qn, preset

  // Notes on the sheet:
  //   Attention, votre version de Logisim
  //   ne contient pas de tracker. Si vous
  //   enregistrez votre projet, toutes les
  //   informations du tracker seront
  //   définitivement effacées.
endmodule

module COUNT_4BITS (
  input  A,
  input  CLR,
  input  CLK,
  output [1:0] D,
  output MAX
);

  wire COUNT_BASE_1_c;

  COUNT_BASE COUNT_BASE_1 (.EN(A), .CLK(CLK), .CLR(CLR), .Q(D[0]), .C(COUNT_BASE_1_c));
  COUNT_BASE COUNT_BASE_2 (.EN(COUNT_BASE_1_c), .CLK(CLK), .CLR(CLR), .Q(D[1]));  // open: C
  and and_1 (MAX, D[0], D[1]);

  // Notes on the sheet:
  //   Attention, votre version de Logisim
  //   ne contient pas de tracker. Si vous
  //   enregistrez votre projet, toutes les
  //   informations du tracker seront
  //   définitivement effacées.
endmodule

module COUNT_8BITS (
  input  A,
  input  CLR,
  input  CLK,
  output [2:0] C,
  output MAX
);

  wire COUNT_BASE_1_c, COUNT_BASE_2_c;

  COUNT_BASE COUNT_BASE_1 (.EN(A), .CLK(CLK), .CLR(CLR), .Q(C[0]), .C(COUNT_BASE_1_c));
  COUNT_BASE COUNT_BASE_2 (.EN(COUNT_BASE_1_c), .CLK(CLK), .CLR(CLR), .Q(C[1]), .C(COUNT_BASE_2_c));
  COUNT_BASE COUNT_BASE_3 (.EN(COUNT_BASE_2_c), .CLK(CLK), .CLR(CLR), .Q(C[2]));  // open: C
  and and_1 (MAX, C[0], C[1], C[2]);

  // Notes on the sheet:
  //   Attention, votre version de Logisim
  //   ne contient pas de tracker. Si vous
  //   enregistrez votre projet, toutes les
  //   informations du tracker seront
  //   définitivement effacées.
endmodule

module REGI_4BITS (
  input  [3:0] D,
  input  S,
  input  CLR,
  input  CLK,
  output [3:0] Q
);

  wire multiplexer_1_out, multiplexer_2_out, multiplexer_3_out, multiplexer_4_out;

  D_Flip_Flop d_ff_1 (.D(multiplexer_1_out), .clk(CLK), .Q(Q[3]), .reset(CLR));  // open: Qn, preset
  Multiplexer #(.enable("false")) multiplexer_1 (.in0(Q[3]), .in1(D[3]), .out(multiplexer_1_out), .sel(S));
  Multiplexer #(.enable("false")) multiplexer_2 (.in0(Q[2]), .in1(D[2]), .out(multiplexer_2_out), .sel(S));
  D_Flip_Flop d_ff_2 (.D(multiplexer_2_out), .clk(CLK), .Q(Q[2]), .reset(CLR));  // open: Qn, preset
  Multiplexer #(.enable("false")) multiplexer_3 (.in0(Q[1]), .in1(D[1]), .out(multiplexer_3_out), .sel(S));
  D_Flip_Flop d_ff_3 (.D(multiplexer_3_out), .clk(CLK), .Q(Q[1]), .reset(CLR));  // open: Qn, preset
  Multiplexer #(.enable("false")) multiplexer_4 (.in0(Q[0]), .in1(D[0]), .out(multiplexer_4_out), .sel(S));
  D_Flip_Flop d_ff_4 (.D(multiplexer_4_out), .clk(CLK), .Q(Q[0]), .reset(CLR));  // open: Qn, preset

  // Notes on the sheet:
  //   Attention, votre version de Logisim
  //   ne contient pas de tracker. Si vous
  //   enregistrez votre projet, toutes les
  //   informations du tracker seront
  //   définitivement effacées.
endmodule

module CHRONO_COUNT_4BITS (
  output [1:0] D,
  output MAX
);

  wire CLK_out;

  Counter #(.width(4), .max('hf)) counter_1 (
    .clr(1'b0), .load(1'b0), .up(1'b1), .count(1'b1), .clk(CLK_out));  // open: D, carry, Q
  Clock CLK (.out(CLK_out));
  Clock sysclk ();  // open: out
  COUNT_4BITS count_4bits_1 (.A(1'b1), .CLK(CLK_out), .D(D), .MAX(MAX));  // open: CLR

  // Notes on the sheet:
  //   Attention, votre version de Logisim
  //   ne contient pas de tracker. Si vous
  //   enregistrez votre projet, toutes les
  //   informations du tracker seront
  //   définitivement effacées.
endmodule

module CHRONO_COUNT_8BITS (
  output [2:0] D,
  output MAX
);

  wire CLK_out;

  Counter #(.width(3), .max('h7)) counter_1 (
    .clr(1'b0), .load(1'b0), .up(1'b1), .count(1'b1), .clk(CLK_out));  // open: D, carry, Q
  Clock CLK (.out(CLK_out));
  Clock sysclk ();  // open: out
  COUNT_8BITS count_8bits_1 (.A(1'b1), .CLK(CLK_out), .C(D), .MAX(MAX));  // open: CLR

  // Notes on the sheet:
  //   Attention, votre version de Logisim
  //   ne contient pas de tracker. Si vous
  //   enregistrez votre projet, toutes les
  //   informations du tracker seront
  //   définitivement effacées.
endmodule

module CHRONO_SHREGI_8BITS (
  input  [1:0] in_1,
  output [7:0] Q
);

  wire CLK_out;
  wire [7:0] counter_1_q;

  Counter counter_1 (
    .clr(1'b0), .load(1'b0), .up(1'b1), .count(1'b1), .clk(CLK_out), .Q(counter_1_q));  // open: D, carry
  Clock CLK (.out(CLK_out));
  Clock sysclk ();  // open: out
  SHREGI_8BITS shregi_8bits_1 (.L(1'b0), .S(in_1), .D(counter_1_q), .R(1'b1), .CLK(CLK_out), .Q(Q));  // open: CLR

  // Notes on the sheet:
  //   Attention, votre version de Logisim
  //   ne contient pas de tracker. Si vous
  //   enregistrez votre projet, toutes les
  //   informations du tracker seront
  //   définitivement effacées.
endmodule

module STAMAC (
  input  START_BIT,
  input  COUNT_8BITS_MAX,
  input  COUNT_4BITS_MAX,
  input  CLR,
  input  CLK,
  output D
);

  wire and_1_out, and_2_out, s_r_ff_1_q, s_r_ff_2_q, xor_1_out;

  and and_1 (and_1_out, COUNT_4BITS_MAX, COUNT_8BITS_MAX);
  and and_2 (and_2_out, COUNT_4BITS_MAX, START_BIT);
  S_R_Flip_Flop #(.trigger("falling")) s_r_ff_1 (
    .S(and_2_out), .R(1'b0), .clk(CLK), .Q(s_r_ff_1_q), .reset(CLR));  // open: Qn, preset
  S_R_Flip_Flop #(.trigger("falling")) s_r_ff_2 (
    .S(and_1_out), .R(1'b0), .clk(CLK), .Q(s_r_ff_2_q), .reset(CLR));  // open: Qn, preset
  xor xor_1 (xor_1_out, s_r_ff_1_q, s_r_ff_2_q);
  Multiplexer #(.enable("false")) multiplexer_1 (.in0(1'b0), .in1(xor_1_out), .out(D), .sel(COUNT_4BITS_MAX));

  // Notes on the sheet:
  //   Attention, votre version de Logisim
  //   ne contient pas de tracker. Si vous
  //   enregistrez votre projet, toutes les
  //   informations du tracker seront
  //   définitivement effacées.
endmodule

module UART (
  input  A,
  input  CLR,
  output [7:0] out_3,
  output [7:0] D
);

  wire COUNT_4BITS_1_max, COUNT_8BITS_1_max, start_bit_1_start, sysclk_out;
  wire [1:0] COUNT_4BITS_1_d;
  wire [1:1] STAMAC_1_d;
  wire [7:0] bit_extender_1_out;

  Clock sysclk (.out(sysclk_out));
  COUNT_4BITS COUNT_4BITS_1 (.A(1'b1), .CLR(CLR), .CLK(sysclk_out), .D(COUNT_4BITS_1_d), .MAX(COUNT_4BITS_1_max));
  assign bit_extender_1_out = {{7{A}}, A};  // Bit_Extender bit_extender_1
  START_BIT start_bit_1 (.CPT4(COUNT_4BITS_1_d), .A(A), .CLK(sysclk_out), .START(start_bit_1_start));
  COUNT_8BITS COUNT_8BITS_1 (.A(STAMAC_1_d[1]), .CLR(CLR), .CLK(sysclk_out), .MAX(COUNT_8BITS_1_max));  // open: C
  STAMAC STAMAC_1 (
    .START_BIT(start_bit_1_start), .COUNT_8BITS_MAX(COUNT_8BITS_1_max), .COUNT_4BITS_MAX(COUNT_4BITS_1_max),
    .CLR(CLR), .CLK(sysclk_out), .D(STAMAC_1_d[1]));
  SHREGI_8BITS SHREGI_8BITS_1 (
    .L(1'b0), .S({2{STAMAC_1_d[1]}}), .D(bit_extender_1_out), .R(A), .CLK(sysclk_out), .CLR(CLR), .Q(out_3));
  REGI_8BITS REGI_8BITS_1 (.S(COUNT_8BITS_1_max), .A(out_3), .CLR(CLR), .CLK(sysclk_out), .Q(D));

  // Notes on the sheet:
  //   Attention, votre version de Logisim
  //   ne contient pas de tracker. Si vous
  //   enregistrez votre projet, toutes les
  //   informations du tracker seront
  //   définitivement effacées.
endmodule

module REGI_8BITS (
  input  S,
  input  [7:0] A,
  input  CLR,
  input  CLK,
  output [7:0] Q
);

  REGI_4BITS REGI_4BITS_1 (.D(A[3:0]), .S(S), .CLR(CLR), .CLK(CLK), .Q(Q[3:0]));
  REGI_4BITS REGI_4BITS_2 (.D(A[7:4]), .S(S), .CLR(CLR), .CLK(CLK), .Q(Q[7:4]));

  // Notes on the sheet:
  //   Attention, votre version de Logisim
  //   ne contient pas de tracker. Si vous
  //   enregistrez votre projet, toutes les
  //   informations du tracker seront
  //   définitivement effacées.
endmodule

module START_BIT (
  input  [1:0] CPT4,
  input  A,
  input  CLK,
  output START
);

  wire and_1_out, and_2_out, and_3_out, nor_1_out, not_1_out, not_2_out, s_r_ff_1_q, s_r_ff_2_q;

  not not_1 (not_1_out, CPT4[1]);
  nor nor_1 (nor_1_out, CPT4[0], CPT4[1]);
  not not_2 (not_2_out, A);
  and and_1 (and_1_out, not_1_out, A);
  S_R_Flip_Flop s_r_ff_1 (.S(and_1_out), .R(1'b0), .clk(CLK), .Q(s_r_ff_1_q), .reset(nor_1_out));  // open: Qn, preset
  and and_2 (and_2_out, not_2_out, CPT4[1]);
  S_R_Flip_Flop s_r_ff_2 (.S(and_2_out), .R(1'b0), .clk(CLK), .Q(s_r_ff_2_q), .reset(nor_1_out));  // open: Qn, preset
  and and_3 (and_3_out, s_r_ff_1_q, s_r_ff_2_q);
  S_R_Flip_Flop s_r_ff_3 (.S(and_3_out), .R(1'b0), .clk(CLK), .Q(START));  // open: reset, Qn, preset

  // Notes on the sheet:
  //   Attention, votre version de Logisim
  //   ne contient pas de tracker. Si vous
  //   enregistrez votre projet, toutes les
  //   informations du tracker seront
  //   définitivement effacées.
endmodule

module oldstart (
);

  wire and_1_out, and_2_out, and_3_out, E2_out, nor_1_out, not_1_out, not_2_out, s_r_ff_1_q, s_r_ff_2_q,
       undriven, undriven_2, undriven_3, undriven_4, undriven_5;

  not not_1 (not_1_out, undriven);
  and E2 (E2_out, undriven_2, not_1_out);
  nor nor_1 (nor_1_out, undriven_2, undriven);
  and and_1 (and_1_out, undriven_5, E2_out);
  and and_2 (and_2_out, undriven_5, undriven_4);
  S_R_Flip_Flop s_r_ff_1 (
    .S(undriven_3), .R(1'b0), .clk(and_1_out), .Q(s_r_ff_1_q), .reset(nor_1_out));  // open: Qn, preset
  not not_2 (not_2_out, undriven_3);
  S_R_Flip_Flop s_r_ff_2 (
    .S(not_2_out), .R(1'b0), .clk(and_2_out), .Q(s_r_ff_2_q), .reset(nor_1_out));  // open: Qn, preset
  and and_3 (and_3_out, s_r_ff_1_q, s_r_ff_2_q);
  S_R_Flip_Flop s_r_ff_3 (.S(and_3_out), .R(1'b0), .clk(undriven_5));  // open: Q, reset, Qn, preset

  // Notes on the sheet:
  //   Attention, votre version de Logisim
  //   ne contient pas de tracker. Si vous
  //   enregistrez votre projet, toutes les
  //   informations du tracker seront
  //   définitivement effacées.
endmodule
